# Fritzing sketch value_from_serial (saved by Fritzing 0.9.9b)
breadboards: 1

parts:
  Part1 = Arduino Uno (Rev3) - ICSP
  12V = Power plug
  Pololu_A2 = Pololu A4988 [package=SO16]
  M2 = Stepper Motor - Bipolar
  C3 = Electrolytic Capacitor [capacitance=100µF voltage=35V package="200 mil [THT, electrolytic]"]

nets:
  N1: Part1.D8, Pololu_A2.DIR
  N2: Part1.D9_PWM, Pololu_A2.STEP
  5V: Part1.5V, Pololu_A2.MS1, Pololu_A2.MS2, Pololu_A2.MS3, Pololu_A2.VDD
  N3: Part1.GND, Pololu_A2.GND#8
  N4: 12V.GND, Pololu_A2.GND#14, C3.-
  N5: 12V.VCC, Pololu_A2.VMOT, C3.+
  N6: Pololu_A2.RESET, Pololu_A2.SLEEP
  N7: Pololu_A2.1B, M2.D
  N8: Pololu_A2.1A, M2.B
  N9: Pololu_A2.2A, M2.C
  N10: Pololu_A2.2B, M2.A

notes:
  (8V to 35V)
