# Fritzing sketch value_from_serial (saved by Fritzing 0.9.9b)

parts:
  Part1 = Arduino Uno (Rev3) - ICSP
  X1 = X113647 Stepper Driver Board [part_number=X113647 package=board]
  MOTOR1 = 28BYJ-48 Stepper Motor
  Power_plug1 = Power plug

nets:
  N1: Part1.D8, X1.IN4
  N2: Part1.D9_PWM, X1.IN3
  N3: Part1.D10_PWM/SS, X1.IN2
  N4: Part1.D11_PWM/MOSI, X1.IN1
  GND: X1.GND, Power_plug1.GND
  N5: X1.+V, Power_plug1.VCC
  N6: X1.BLUE, MOTOR1.BLUE
  N7: X1.PINK, MOTOR1.PINK
  N8: X1.YELLOW, MOTOR1.RED
  N9: X1.ORANGE, MOTOR1.ORANGE
  N10: X1.RED, MOTOR1.YELLOW

custom parts:
  X113647 Stepper Driver Board: A common stepper motor driver board based on ULN2003APG darlington array
  28BYJ-48 Stepper Motor: 28BYJ-48 gear-reduction stepper motor (small)
